// Logisim project Test.circ as structural Verilog: 1 circuit, main circuit main
module main (
);

  wire button_1_out, ide_memory_card_1_p2, ide_memory_card_1_p3;

  Button button_1 (.out(button_1_out));
  // IDE_Memory_Card ide_memory_card_1: pin names not known; wires that end beside it: button_1_out, ide_memory_card_1_p2, ide_memory_card_1_p3, ide_memory_card_1_p3, ide_memory_card_1_p2
endmodule
